# Fritzing sketch final (saved by Fritzing 0.9.3b)

parts:
  Arduino_Uno = Arduino Uno (Rev3)
  Raspberry_Pi_1 = Raspberry Pi 3 [part_number=RPI-3-V1.2]
  Level_Shifter = Logic Level Converter
  V1 = DC Power [voltage=5]
  Relay = RELAY [package=relay-t9a]
  Relay_2 = RELAY [package=relay-t9a]
  Relay_3 = RELAY [package=relay-t9a]
  V2 = AC Power [voltage=230 frequency=50]
  Transformer_230V_12V = Transformer [package=transformer]
  Transformer_230V_12V_2 = Transformer [package=transformer]
  Transformer_230V_12V_3 = Transformer [package=transformer]
  Red = Bulb holder (E10) with base
  Amber = Bulb holder (E10) with base
  Green = Bulb holder (E10) with base

nets:
  N1: Arduino_Uno.A4/SDA, Level_Shifter.TX_HV
  N2: Arduino_Uno.A5/SCL, Level_Shifter.TX2_HV
  N3: Arduino_Uno.D8, Relay.COIL1
  N4: Arduino_Uno.D9_PWM, Relay_2.COIL1
  N5: Arduino_Uno.D10_PWM/SS, Relay_3.COIL1
  GND: Arduino_Uno.GND, Raspberry_Pi_1.GND, Level_Shifter.GND, V1.V-, Relay.COIL2, Relay_2.COIL2, Relay_3.COIL2
  N6: Arduino_Uno.5V, Level_Shifter.HV
  VIN: Arduino_Uno.VIN, Raspberry_Pi_1.5V, V1.V+
  N7: Raspberry_Pi_1.GPIO2, Level_Shifter.RX_HV
  N8: Raspberry_Pi_1.GPIO3, Level_Shifter.RX2_HV
  N9: Raspberry_Pi_1.3V3, Level_Shifter.LV
  N10: Relay.MAIN, Relay_2.MAIN, Relay_3.MAIN, V2.V+
  N11: Relay.NO, Transformer_230V_12V_3.1
  N12: Relay_2.NO, Transformer_230V_12V_2.1
  N13: Relay_3.NO, Transformer_230V_12V.1
  N14: V2.V-, Transformer_230V_12V.2, Transformer_230V_12V_2.2, Transformer_230V_12V_3.2
  N15: Transformer_230V_12V.3, Green.pin_2
  N16: Transformer_230V_12V.4, Green.pin_1
  N17: Transformer_230V_12V_2.3, Amber.pin_2
  N18: Transformer_230V_12V_2.4, Amber.pin_1
  N19: Transformer_230V_12V_3.3, Red.pin_2
  N20: Transformer_230V_12V_3.4, Red.pin_1

custom parts:
  Bulb holder (E10) with base: A bulb holder for an E10 bulb with a base.
