# Fritzing sketch leds (saved by Fritzing 0.9.3b)

parts:
  Arduino_Uno = Arduino Uno (Rev3)
  V1 = DC Power [voltage=5]
  Red = LEDs [package=led10mm]
  R1 = Resistor [tolerance=±5% resistance=470 package=THT]
  Amber = LEDs [package=led10mm]
  Green = LEDs [package=led10mm]
  R2 = Resistor [tolerance=±5% resistance=470 package=THT]
  R3 = Resistor [tolerance=±5% resistance=470 package=THT]

nets:
  N1: Arduino_Uno.D8, R3.Pin_0
  N2: Arduino_Uno.D9_PWM, R2.Pin_0
  N3: Arduino_Uno.D10_PWM/SS, R1.Pin_0
  N4: Arduino_Uno.GND, V1.V-, Red.C, Amber.C, Green.C
  N5: Arduino_Uno.VIN, V1.V+
  N6: Red.A, R3.Pin_1
  N7: R1.Pin_1, Green.A
  N8: Amber.A, R2.Pin_1
