# Fritzing sketch relays (saved by Fritzing 0.9.3b)

parts:
  Arduino_Uno = Arduino Uno (Rev3)
  V1 = DC Power [voltage=5]
  Relay = RELAY [package=relay-t9a]
  Relay_2 = RELAY [package=relay-t9a]
  Relay_3 = RELAY [package=relay-t9a]

nets:
  N1: Arduino_Uno.D8, Relay.COIL1
  N2: Arduino_Uno.D9_PWM, Relay_2.COIL1
  N3: Arduino_Uno.D10_PWM/SS, Relay_3.COIL1
  N4: Arduino_Uno.GND, V1.V-, Relay.COIL2, Relay_2.COIL2, Relay_3.COIL2
  N5: Arduino_Uno.VIN, V1.V+
