# Fritzing sketch relaysLeds (saved by Fritzing 0.9.3b)

parts:
  Arduino_Uno = Arduino Uno (Rev3)
  V1 = DC Power [voltage=5]
  Relay = RELAY [package=relay-t9a]
  Relay_2 = RELAY [package=relay-t9a]
  Relay_3 = RELAY [package=relay-t9a]
  Red = LEDs [package=led10mm]
  Amber = LEDs [package=led10mm]
  Green = LEDs [package=led10mm]
  R1 = Resistor [tolerance=±5% resistance=470 package=THT]
  R2 = Resistor [tolerance=±5% resistance=470 package=THT]
  R3 = Resistor [tolerance=±5% resistance=470 package=THT]

nets:
  N1: Arduino_Uno.D8, Relay.COIL1
  N2: Arduino_Uno.D9_PWM, Relay_2.COIL1
  N3: Arduino_Uno.D10_PWM/SS, Relay_3.COIL1
  N4: Arduino_Uno.GND, V1.V-, Relay.COIL2, Relay_2.COIL2, Relay_3.COIL2, Red.C, Amber.C, Green.C
  N5: Arduino_Uno.VIN, V1.V+, Relay.MAIN, Relay_2.MAIN, Relay_3.MAIN
  N6: Relay.NO, R1.Pin_0
  N7: Relay_2.NO, R2.Pin_0
  N8: Relay_3.NO, R3.Pin_0
  N9: Red.A, R1.Pin_1
  N10: Amber.A, R2.Pin_1
  N11: Green.A, R3.Pin_1
