# Fritzing sketch relaysMains (saved by Fritzing 0.9.3b)

parts:
  Arduino_Uno = Arduino Uno (Rev3)
  V1 = DC Power [voltage=5]
  Relay = RELAY [package=relay-t9a]
  Relay_2 = RELAY [package=relay-t9a]
  Relay_3 = RELAY [package=relay-t9a]
  V2 = AC Power [voltage=230 frequency=50]
  Transformer_230V_12V = Transformer [package=transformer]
  Transformer_230V_12V_2 = Transformer [package=transformer]
  Transformer_230V_12V_3 = Transformer [package=transformer]
  Red = Bulb holder (E10) with base
  Amber = Bulb holder (E10) with base
  Green = Bulb holder (E10) with base

nets:
  N1: Arduino_Uno.D8, Relay.COIL1
  N2: Arduino_Uno.D9_PWM, Relay_2.COIL1
  N3: Arduino_Uno.D10_PWM/SS, Relay_3.COIL1
  N4: Arduino_Uno.GND, V1.V-, Relay.COIL2, Relay_2.COIL2, Relay_3.COIL2
  N5: Arduino_Uno.VIN, V1.V+
  N6: Relay.MAIN, Relay_2.MAIN, Relay_3.MAIN, V2.V+
  N7: Relay.NO, Transformer_230V_12V_3.1
  N8: Relay_2.NO, Transformer_230V_12V_2.1
  N9: Relay_3.NO, Transformer_230V_12V.1
  N10: V2.V-, Transformer_230V_12V.2, Transformer_230V_12V_2.2, Transformer_230V_12V_3.2
  N11: Transformer_230V_12V.3, Green.pin_2
  N12: Transformer_230V_12V.4, Green.pin_1
  N13: Transformer_230V_12V_2.3, Amber.pin_2
  N14: Transformer_230V_12V_2.4, Amber.pin_1
  N15: Transformer_230V_12V_3.3, Red.pin_2
  N16: Transformer_230V_12V_3.4, Red.pin_1

custom parts:
  Bulb holder (E10) with base: A bulb holder for an E10 bulb with a base.
